# Fritzing sketch sch (saved by Fritzing 0.9.3b)
breadboards: 1

parts:
  Part2 = Tri-Axis Gyro Breakout - L3G4200D
  USB1 = Wiring USB Adapter
  R1 = Resistor [tolerance=±5% resistance=4.7k package=THT]
  D1 = Rectifier Diode [part_number=1N4001 package="300 mil [THT]"]
  XTAL1 = Crystal [frequency="16 Mhz" package=SMD]

nets:
  GND: Part2.GND, USB1.GND
  VCC: Part2.VCC, USB1.3.3V, R1.Pin_0
  N1: Part2.SCL, USB1.TX
  N2: Part2.SDA, USB1.RX, R1.Pin_1, D1.anode
  N3: USB1.RTS, D1.cathode
  N4: USB1.OSCI, XTAL1.pin_0
  N5: USB1.OSCO, XTAL1.pin_1

notes:
  12MHz
